# Fritzing sketch schematic (saved by Fritzing 0.9.6b)
perfboards: 1

parts:
  Part1 = Arduino Nano (Rev3.0) (ICSP)
  MD03A1 = Dual VNH2SP30 Motor Driver [part_number=MD03A]
  M1 = RioRand LM2596
  Enc1 = shaft encoder
  Enc2 = shaft encoder
  BAT1 = LIPO-2000mAh [package=lipo-2000]
  J1 = Basic Servo
  M2 = DC Motor
  Enc3 = shaft encoder
  Enc4 = shaft encoder
  R4 = Resistor [tolerance=±5% resistance=10k package="0402 [SMD]"]
  R5 = Resistor [tolerance=±5% resistance=10k package="0402 [SMD]"]
  R6 = Resistor [tolerance=±5% resistance=10k package="0402 [SMD]"]
  R7 = Resistor [tolerance=±5% resistance=10k package="0402 [SMD]"]
  R8 = Resistor [tolerance=±5% resistance=220 package="0402 [SMD]"]

nets:
  GND: Part1.GND, M1.Pin_4, J1.gnd
  N1: Part1.D9, J1.pulse
  N2: Part1.D10, MD03A1.1INb
  N3: Part1.D11/MOSI, MD03A1.PWM
  N4: Part1.D12/MISO, MD03A1.1INa
  VIN: Part1.VIN, M1.Pin_3, J1.vcc
  N5: Part1.5V, MD03A1.+5V_(IN)
  N6: MD03A1.GND, R4.Pin_1, R5.Pin_1, R6.Pin_1, R7.Pin_1
  N7: MD03A1.OUT_1A, M2.pin_2
  N8: MD03A1.OUT_1B, M2.pin_1
  N9: M1.Pin_1, BAT1.+
  N10: M1.Pin_2, BAT1.-
  VCC: Enc1.VCC, Enc2.VCC, Enc3.VCC, Enc4.VCC, R8.Pin_0
  N11: Enc1.OUT, R7.Pin_0
  N12: Enc2.OUT, R5.Pin_0
  N13: Enc3.OUT, R4.Pin_0
  N14: Enc4.OUT, R6.Pin_0
